# Fritzing sketch montage elec (saved by Fritzing 0.9.3b)
breadboards: 1

parts:
  M1 = Dagu DGServo 9g (Top view) [part_number=RS001B]
  M2 = Dagu DGServo 9g (Top view) [part_number=RS001B]
  VCC1 = 4 x AAA Battery Mount  # not connected
  IC2 = ULN2803A [package=THT]  # not connected
  IC3 = ULN2803A [package=THT]  # not connected
  IC4 = ULN2803A [package=THT]  # not connected
  U2 = Voltage Regulator - 5V [package="DPak [SMD]"]
  U3 = Voltage Regulator - 5V [package="DPak [SMD]"]  # not connected
  S1 = Taiway 100-SP-X-T1 SPDT Miniature Toggle Switch [part_number=100-SP-X-T1-0-0-B1-M1 package=THT]  # not connected
  IC5 = L293D [package=THT]
  IC6 = L293D [package=THT]
  Composant1 = Arduino Uno (Rev3)
  IC7 = PICAXE-28X2 [package=THT]  # not connected
  IC8 = PICAXE-18 [package=THT]  # not connected
  M4 = Stepper Motor - Bipolar
  M5 = Stepper Motor - Bipolar
  hc-sr1 = hc-sr04
  M6 = Stepper Motor - Bipolar
  M7 = Stepper Motor - Bipolar
  L1 = Solenoid
  D1 = Rectifier Diode [part_number=1N4001 package="Melf DO-213 AB [SMD]"]
  R1 = Resistor [tolerance=±5% resistance=220 package="2010 [SMD]"]

nets:
  N1: M1.gnd, Composant1.D9_PWM
  VCC: M1.vcc, M2.vcc, IC5.+V, IC6.+V, Composant1.5V, hc-sr1.VCC
  GND: M1.pulse, M2.pulse, U2.output_voltage, IC5.0V, IC6.0V, Composant1.GND, hc-sr1.GND
  N2: M2.gnd, Composant1.D10_PWM/SS
  N3: U2.GND, L1.pin1, D1.anode
  N4: IC5.Enable_1, IC6.Enable_1, Composant1.D6_PWM
  N5: IC5.In_1, IC6.In_1, Composant1.D13/SCK, R1.Pin_0
  N6: IC5.Out_1_(_Controlled_by_Enable_1_), M7.C
  N7: IC5.Out_2_(_Controlled_by_Enable_1_), M7.B
  N8: IC5.In_2, IC6.In_2, Composant1.D12/MISO
  N9: IC5.Enable_2, IC6.Enable_2, Composant1.D3_PWM
  N10: IC5.In_3, IC6.In_3, Composant1.D7
  N11: IC5.Out_3_(_Controlled_by_Enable_2_), M5.B
  N12: IC5.Out_4_(_Controlled_by_Enable_2_), M5.C
  N13: IC5.In_4, IC6.In_4, Composant1.D4
  N14: IC6.Out_1_(_Controlled_by_Enable_1_), M6.C
  N15: IC6.Out_2_(_Controlled_by_Enable_1_), M6.B
  N16: IC6.+Vmotor, L1.pin2, D1.cathode
  N17: IC6.Out_3_(_Controlled_by_Enable_2_), M4.B
  N18: IC6.Out_4_(_Controlled_by_Enable_2_), M4.C
  N19: Composant1.A0, hc-sr1.Trig

// code stored in the sketch: Untitled2.ino
run
